# Fritzing sketch raspiviv (saved by Fritzing 0.9.3b)
breadboards: 1

parts:
  Raspberry_Pi_1 = Raspberry Pi 2
  LED27 = LED - 5mm [color="Green (555nm)" package="5 mm [THT]"]
  R2 = Resistor [tolerance=±5% resistance=220 package=THT]  # not connected
  R3 = Resistor [tolerance=±5% resistance=2.2k package=THT]
  Q3 = NPN-Transistor [package="SOT-23 [SMD]"]
  JP1 = Header 3 [package=molex-1x3_lock]  # not connected
  JP2 = Header 3 [package=molex-1x3_lock]
  R4 = Trimmer Potentiometer [maximum_resistance=10kΩ package=THT]
  S1 = Toggle Switch [package=THT]

nets:
  N1: Raspberry_Pi_1.GPIO24, JP2.1
  N2: Raspberry_Pi_1.GND, JP2.3
  N3: Raspberry_Pi_1.5V, JP2.2
  N4: LED27.cathode, LED27.anode, S1.L1, S1.COM, S1.L2
  N5: R3.Pin_0, R3.Pin_1, Q3.2, Q3.1, R4.leg1, R4.wiper
